# Fritzing sketch sketch (saved by Fritzing 0.9.9b)

parts:
  Mod1 = Microbit
  KF-1 = KF-301 Relay [package=THT]
  J1 = Piezo Speaker
  BAT1 = 12 battery [package=battery]
  USBTTL1 = USB A Plug
  USBTTL2 = Micro USB B Plug

nets:
  N1: Mod1.P2, KF-1.signal
  N2: Mod1.GND, KF-1.ground
  N3: KF-1.C, BAT1.-
  N4: KF-1.NO, J1.pin1
  N5: J1.pin2, BAT1.+
  N6: USBTTL1.usb, USBTTL2.usb

notes:
  Power from cigarette lighter socket charger which converts 12 volts from car battery below to 5 volts.
  microUSB cables supplies 5 volts bit internally micro:bit converts it to 3.3 volts
  12 volts car battery. Should also be connected to some solar charging circuit
  12 volts Hooter
  The relay helps isolate 3.3 volts signal from micro:bit from the 12 volts required to sound the hooter. The relay's coil might need 5 volts, so opto-isolated version is better so that 3.3 volts can be used to activate the isolator.
  BBC micro:bit has a sketch running that turns the relay on when the board tilts beyond the threshold (uses on-board accelerometer)

custom parts:
  Microbit: BBC Microbit Fritzing part. May 2019 expanded to include schematic and pcb views as well as breadboard. PCB view assumes an Adafruit PRODUCT ID: 3342 2x40 Right Angle through hole edge connector (although others will probably work as well). The pcb svg is custom (see forum article http://forum.fritzing.org/t/making-edge-connectors-and-both-side-smd-parts/7287 for an explaination if you need to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
  KF-301 Relay: KF-301
  12 battery: 12V lead acid type battery, like the Husqvarna YTH2448 12V 35AH battery. This is the mini version 1/4 the size of the actual battery to be closer to typical breadboard parts (around 2in wide rathher than 7in). The pads in pcb are sized to accomidate up to 14ga wire (as these batterys will deliver high currents.)
